# Fritzing sketch I2C (saved by Fritzing 0.9.5d)
breadboards: 1

parts:
  Part1 = Arduino Uno (Rev3)
  Part2 = Arduino Uno (Rev3)
  Part3 = Arduino Uno (Rev3)
  LED1 = LED - 5mm [color="Red (633nm)" package="5 mm [THT]"]
  LED2 = LED - 5mm [color="Green (560nm)" package="5 mm [THT]"]
  LED3 = LED - 5mm [color="Yellow (585nm)" package="5 mm [THT]"]
  R1 = Resistor [tolerance=±5% resistance=220 package=THT]
  R2 = Resistor [tolerance=±5% resistance=220 package=THT]
  R3 = Resistor [tolerance=±5% resistance=220 package=THT]
  LED4 = LED - 5mm [color="Red (633nm)" package="5 mm [THT]"]
  LED5 = LED - 5mm [color="Yellow (585nm)" package="5 mm [THT]"]
  LED6 = LED - 5mm [color="Green (560nm)" package="5 mm [THT]"]
  R4 = Resistor [tolerance=±5% resistance=220 package=THT]
  R5 = Resistor [tolerance=±5% resistance=220 package=THT]
  R6 = Resistor [tolerance=±5% resistance=220 package=THT]
  S1 = Pushbutton [package="[THT]"]
  S2 = Pushbutton [package="[THT]"]

nets:
  N1: Part1.A4/SDA, Part2.A4/SDA, Part3.A4/SDA
  N2: Part1.A5/SCL, Part2.A5/SCL, Part3.A5/SCL
  GND: Part1.GND, Part2.GND, Part3.GND, R2.Pin_1, R3.Pin_1, R5.Pin_0, R6.Pin_0, S1.Pin_3, S1.Pin_4, S2.Pin_3, S2.Pin_4
  N3: Part1.D2, LED4.anode
  N4: Part1.D3_PWM, LED5.anode
  N5: Part1.D4, LED6.anode
  N6: Part1.D6_PWM, S2.Pin_1, S2.Pin_2
  N7: Part2.D2, LED1.anode
  N8: Part2.D3_PWM, LED3.anode
  N9: Part2.D4, LED2.anode
  N10: Part2.D6_PWM, S1.Pin_1, S1.Pin_2
  N11: LED1.cathode, R1.Pin_0
  N12: LED2.cathode, R3.Pin_0
  N13: LED3.cathode, R2.Pin_0
  N14: LED4.cathode, R4.Pin_1
  N15: LED5.cathode, R5.Pin_1
  N16: LED6.cathode, R6.Pin_1
