# Fritzing sketch Rotary_Encoder (saved by Fritzing 0.9.5d)
breadboards: 1

parts:
  S1 = Pushbutton [package="[THT]"]
  S2 = Pushbutton [package="[THT]"]
  S3 = Pushbutton [package="[THT]"]
  S4 = Pushbutton [package="[THT]"]
  RE1 = Rotary Encoder [package=THT]
  Part1 = Arduino Uno (Rev3)
  R1 = Resistor [tolerance=±5% resistance=220 package=THT]
  R2 = Resistor [tolerance=±5% resistance=220 package=THT]
  R3 = Resistor [tolerance=±5% resistance=220 package=THT]
  LED2 = RGB LED (com. anode, rbg) [package="5 mm [THT]"]

nets:
  N1: S1.Pin_1, S1.Pin_2, S2.Pin_1, S2.Pin_2, S3.Pin_1, S3.Pin_2, S4.Pin_3, S4.Pin_4, Part1.GND
  N2: S1.Pin_3, S1.Pin_4, Part1.D7
  N3: S2.Pin_3, S2.Pin_4, Part1.D4
  N4: S3.Pin_3, S3.Pin_4, Part1.D3_PWM
  N5: S4.Pin_1, S4.Pin_2, Part1.D2
  N6: RE1.EncoderPinA, Part1.D12/MISO
  N7: RE1.EncoderPinC, Part1.D11_PWM/MOSI
  N8: Part1.D9_PWM, R3.Pin_0
  N9: Part1.D5_PWM, R1.Pin_0
  N10: Part1.D6_PWM, R2.Pin_0
  N11: Part1.5V, LED2.common_anode
  N12: R1.Pin_1, LED2.green_cathode
  N13: R2.Pin_1, LED2.blue_cathode
  N14: R3.Pin_1, LED2.red_cathode

notes:
  Clk Pin
  DT Pin
  SW Pin
