# Fritzing sketch LDR (saved by Fritzing 0.9.5d)
breadboards: 1

parts:
  Part1 = Arduino Uno (Rev3)
  S1 = Pushbutton [package="[THT]"]
  S2 = Pushbutton [package="[THT]"]
  R1 = Photocell (LDR) [package=THT]
  R2 = Resistor [tolerance=±5% resistance=1k package=THT]
  R3 = Resistor [tolerance=±5% resistance=1k package="0805 [SMD]"]
  R4 = Resistor [tolerance=±5% resistance=1k package="0805 [SMD]"]
  LED1 = LED - 5mm [color="Red (633nm)" package="5 mm [THT]"]
  LED2 = LED - 5mm [color="Green (565nm)" package="5 mm [THT]"]
  LED3 = LED - 5mm [color="Blue (525nm)" package="5 mm [THT]"]
  R5 = Resistor [tolerance=±5% resistance=330 package=THT]
  R6 = Resistor [tolerance=±5% resistance=220 package=THT]
  R7 = Resistor [tolerance=±5% resistance=220 package=THT]

nets:
  N1: Part1.A0, R1.pin_1, R2.Pin_1
  N2: Part1.A1, R3.Pin_1, R4.Pin_1
  N3: Part1.GND, S2.Pin_3, S2.Pin_4, R2.Pin_0, R5.Pin_0, R7.Pin_0
  N4: Part1.D2, LED1.anode
  N5: Part1.D3_PWM, LED2.anode
  N6: Part1.D4, LED3.anode
  N7: Part1.5V, R1.pin_0, R3.Pin_0
  N8: S1.Pin_1, S1.Pin_2, R4.Pin_0
  N9: S1.Pin_3, S1.Pin_4
  N10: S2.Pin_1, S2.Pin_2
  N11: LED2.cathode, R6.Pin_1
  N12: LED3.cathode, R5.Pin_1
