# Fritzing sketch Proximity alert (saved by Fritzing 0.9.5d)
breadboards: 1

parts:
  S1 = Pushbutton [package="[THT]"]
  LED1 = LED - 5mm [color="Red (633nm)" package="5 mm [THT]"]  # not connected
  LED2 = LED - 5mm [color="Blue (470nm)" package="5 mm [THT]"]
  LED3 = LED - 5mm [color="Yellow (592nm)" package="5 mm [THT]"]
  LED4 = LED - 5mm [color="White (8000K)" package="5 mm [THT]"]
  HC-SR04_Sensor_1 = HC-SR04 Ultrasonic Distance Sensor
  J1 = Piezo Speaker
  R1 = Resistor [tolerance=±5% resistance=220 package=THT]
  R2 = Resistor [tolerance=±5% resistance=220 package=THT]  # not connected
  R3 = Resistor [tolerance=±5% resistance=220 package=THT]
  R4 = Resistor [tolerance=±5% resistance=220 package=THT]
  R5 = Resistor [tolerance=±5% resistance=220 package=THT]
  LED5 = smd LED [color="Red (633nm)" package="0603 [SMD]"]
  LED5_2 = smd LED [color="Green (570nm)" package="1206 [SMD]"]
  Part1 = Arduino Uno (Rev3)

nets:
  N1: S1.Pin_1, S1.Pin_2, LED2.cathode
  N2: S1.Pin_3, S1.Pin_4, J1.pin1, R1.Pin_0, R3.Pin_0, R4.Pin_0, R5.Pin_0, Part1.GND
  N3: LED3.cathode, LED5.cathode, LED5_2.cathode
  VCC: LED3.anode, HC-SR04_Sensor_1.VCC, Part1.5V
  N4: LED4.anode, Part1.D6_PWM
  N5: HC-SR04_Sensor_1.TRIG, Part1.D11_PWM/MOSI
  N6: HC-SR04_Sensor_1.ECHO, Part1.D10_PWM/SS
  N7: J1.pin2, Part1.D2
  N8: LED5.anode, LED5_2.anode, Part1.D7
