# Fritzing sketch Multi_LED_Blink (saved by Fritzing 0.9.5d)
breadboards: 1

parts:
  Part1 = Arduino Uno (Rev3)
  LED1 = LED - 5mm [color="Red (633nm)" package="5 mm [THT]"]
  R1 = Resistor [tolerance=±5% resistance=220 package=THT]
  LED2 = LED - 5mm [color="Blue (470nm)" package="5 mm [THT]"]
  R2 = Resistor [tolerance=±5% resistance=220 package=THT]
  LED3 = LED - 5mm [color="Orange (620nm)" package="5 mm [THT]"]
  R3 = Resistor [tolerance=±5% resistance=220 package=THT]
  LED4 = LED - 5mm [color="White (6500K)" package="5 mm [THT]"]
  R4 = Resistor [tolerance=±5% resistance=220 package=THT]
  LED5 = LED - 5mm [color="Green (570nm)" package="5 mm [THT]"]
  R5 = Resistor [tolerance=±5% resistance=220 package=THT]

nets:
  N1: Part1.D3_PWM, LED5.anode
  N2: Part1.D4, LED4.anode
  N3: Part1.D5_PWM, LED3.anode
  N4: Part1.D6_PWM, LED2.anode
  N5: Part1.D7, LED1.anode
  N6: Part1.GND, R1.Pin_0, R2.Pin_0, R3.Pin_0, R4.Pin_0, R5.Pin_0
  N7: LED1.cathode, R1.Pin_1
  N8: LED2.cathode, R2.Pin_1
  N9: LED3.cathode, R3.Pin_1
  N10: LED4.cathode, R4.Pin_1
  N11: LED5.cathode, R5.Pin_1

// code stored in the sketch: blinky_blinky_code.ino
void setup() {
  for (int i = 7; i >= 2;) {
    pinMode(i, OUTPUT);
    i = i - 1;
  }
}

int delayTime = 300;
void loop() {
    //1
  for (int i = 7; i >= 3;) {
    digitalWrite(i, HIGH);
    i = i - 1;
    delay(delayTime);
  }

  //2
  for (int i = 3; i <= 7;) {
    digitalWrite(i, LOW);
    delay(delayTime);
    i = i + 1;
  }

  //3
  for (int i = 3; i <= 7;) {
    digitalWrite(i, HIGH);
    i = i + 1;
  }
  delay(delayTime);
  for (int i = 3; i <= 7;) {
    digitalWrite(i, LOW);
    i = i + 1;
  }
  delay(delayTime);


  //4
  for (int i = 7; i >= 3;) {
    digitalWrite(i, HIGH);
    delay(delayTime);
    digitalWrite(i, LOW);
    delay(delayTime);
    i = i - 1;
  }

  //5
  for (int i = 4; i <= 7;) {
    digitalWrite(i, HIGH);
    delay(delayTime);
    digitalWrite(i, LOW);
    delay(delayTime);
    i = i + 1;
  }
  
  if(delayTime == 300){
    delayTime = 200;
  }else {
    delayTime = 300;
  }  
}
