# Fritzing sketch RGB Push Button (saved by Fritzing 0.9.5d)
breadboards: 1

parts:
  Part1 = Arduino Uno (Rev3)
  S1 = Pushbutton [package="[THT]"]
  S2 = Pushbutton [package="[THT]"]
  S3 = Pushbutton [package="[THT]"]
  S4 = Pushbutton [package="[THT]"]
  LED1 = RGB LED (com. cathode, rgb) [package="5 mm [THT]"]
  R1 = Resistor [tolerance=±5% resistance=220 package=THT]
  R2 = Resistor [tolerance=±5% resistance=220 package=THT]
  R3 = Resistor [tolerance=±5% resistance=220 package=THT]

nets:
  N1: Part1.D9_PWM, R3.Pin_0
  N2: Part1.D10_PWM/SS, R2.Pin_0
  N3: Part1.D11_PWM/MOSI, R1.Pin_0
  N4: Part1.D4, S4.Pin_1, S4.Pin_2
  N5: Part1.D5_PWM, S3.Pin_1, S3.Pin_2
  N6: Part1.D6_PWM, S2.Pin_1, S2.Pin_2
  N7: Part1.D7, S1.Pin_1, S1.Pin_2
  N8: Part1.5V, LED1.common_cathode
  N9: Part1.GND, S1.Pin_3, S1.Pin_4, S2.Pin_3, S2.Pin_4, S3.Pin_3, S3.Pin_4, S4.Pin_3, S4.Pin_4
  N10: LED1.red_anode, R1.Pin_1
  N11: LED1.green_anode, R2.Pin_1
  N12: LED1.blue_anode, R3.Pin_1
